// Logisim project CEP SCDP modified.circ as structural Verilog: 7 circuits, main circuit main
module main (
  output RegDst,
  output ALUsrc,
  output MemRead,
  output MemToReg,
  output Jump,
  output RegWrite,
  output [1:0] ALUOp,
  output MemWrite,
  output Branch,
  output lwmadd,
  output ZeroFlag,
  output [2:0] ALUOperation,
  output [31:0] out_13,
  output [31:0] out_14,
  output [31:0] out_15,
  output [5:0] out_16,
  output [4:0] out_17,
  output [4:0] out_18,
  output [4:0] out_19,
  output [5:0] out_20,
  output [31:0] out_21,
  output [31:0] out_22,
  output [31:0] out_23,
  output [5:0] out_24,
  output [4:0] out_25,
  output [4:0] out_26,
  output [15:0] out_27,
  output [31:0] out_28,
  output [31:0] out_29,
  output [31:0] out_30,
  output [5:0] out_31,
  output [4:0] out_32,
  output [4:0] out_33,
  output [15:0] out_34,
  output [31:0] out_35,
  output [31:0] out_36,
  output [5:0] out_37,
  output [4:0] out_38,
  output [4:0] out_39,
  output [15:0] out_40,
  output [31:0] out_41,
  output [31:0] out_42,
  output [31:0] out_43,
  output [5:0] out_44,
  output [25:0] out_45
);

  wire and_1_out, clock_1_out;
  wire [27:0] bit_extender_1_out;
  wire [31:0] adder_1_out, adder_2_out, bit_extender_2_out, data_memory_1_readdata, multiplexer_2_out,
       multiplexer_3_out, multiplexer_4_out;

  Register #(.width(32)) PC (.D(out_15), .en(1'b1), .Q(out_14), .clk(clock_1_out));  // open: clr
  Clock clock_1 (.out(clock_1_out));
  Adder #(.width(32)) adder_1 (.a(out_14), .b(32'h1), .out(adder_1_out));  // open: cin, cout
  Instruction_Memory instruction_memory_1 (
    .Clock(clock_1_out), .Enable(1'b1), .Instruction(out_13), .Address(out_14[23:0]));
  assign bit_extender_1_out = {{2{1'b0}}, out_13[25:0]};  // Bit_Extender bit_extender_1
  Control_Unit control_unit_1 (
    .Instruction_31_26(out_13[31:26]), .RegWrite(RegWrite), .ALUsrc(ALUsrc), .MemWrite(MemWrite),
    .Branch(Branch), .RegDst(RegDst), .ALUOp(ALUOp), .MemRead(MemRead), .MemToReg(MemToReg), .Jump(Jump),
    .lwmadd(lwmadd));
  Multiplexer #(.width(5)) multiplexer_1 (
    .in0(out_13[20:16]), .in1(out_13[15:11]), .out(out_19), .sel(RegDst));  // open: en
  assign bit_extender_2_out = {{16{1'b0}}, out_13[15:0]};  // Bit_Extender bit_extender_2
  Register_File register_file_1 (
    .ReadReg1(out_13[25:21]), .ReadReg2(out_13[20:16]), .Write(RegWrite), .Clock(clock_1_out),
    .WriteReg(out_19), .WriteData(out_23), .ReadData1(out_21), .ReadData2(out_22));
  Multiplexer #(.width(32)) multiplexer_2 (
    .in0(out_22), .in1(bit_extender_2_out), .out(multiplexer_2_out), .sel(ALUsrc));  // open: en
  ALU_Control alu_control_1 (.ALUop(ALUOp), .Instruction_5_0(out_13[5:0]), .ALUOperation(ALUOperation));
  ALU alu_1 (
    .ALUOperation(ALUOperation), .Src1(out_21), .Src2(multiplexer_2_out), .Zero_Flag(ZeroFlag),
    .ALU_Result(out_29));
  Multiplexer #(.width(32)) multiplexer_3 (
    .in0(out_29), .in1(bit_extender_2_out), .out(multiplexer_3_out), .sel(lwmadd));  // open: en
  Adder #(.width(32)) adder_2 (.a(adder_1_out), .b(bit_extender_2_out), .out(adder_2_out));  // open: cin, cout
  Data_Memory data_memory_1 (
    .Address(multiplexer_3_out[23:0]), .WriteData(out_22), .ReadData(data_memory_1_readdata),
    .MemWrite(MemWrite), .Clock(clock_1_out), .MemRead(MemRead));
  Multiplexer #(.width(32)) multiplexer_4 (
    .in0(adder_1_out), .in1(adder_2_out), .out(multiplexer_4_out), .sel(and_1_out));  // open: en
  and and_1 (and_1_out, Branch, ZeroFlag);
  Multiplexer #(.width(32)) multiplexer_5 (
    .in0(out_29), .in1(data_memory_1_readdata), .out(out_23), .sel(MemToReg));  // open: en
  Multiplexer #(.width(32)) multiplexer_6 (
    .in0(multiplexer_4_out), .in1({adder_1_out[31:28], bit_extender_1_out}), .out(out_15), .sel(Jump));  // open: en

  assign out_16 = out_13[31:26];
  assign out_17 = out_13[25:21];
  assign out_18 = out_13[20:16];
  assign out_20 = out_13[5:0];
  assign out_24 = out_13[31:26];
  assign out_25 = out_13[25:21];
  assign out_26 = out_19;
  assign out_27 = out_13[15:0];
  assign out_28 = out_21;
  assign out_30 = out_23;
  assign out_31 = out_13[31:26];
  assign out_32 = out_13[25:21];
  assign out_33 = out_19;
  assign out_34 = out_13[15:0];
  assign out_35 = out_21;
  assign out_36 = out_23;
  assign out_37 = out_13[31:26];
  assign out_38 = out_13[25:21];
  assign out_39 = out_13[20:16];
  assign out_40 = out_13[15:0];
  assign out_41 = out_21;
  assign out_42 = out_22;
  assign out_43 = out_29;
  assign out_44 = out_13[31:26];
  assign out_45 = out_13[25:0];

  // Other names for the same wires on the sheet: ALUResult_Address[31:0] = out_29; Func[5:0] = out_13[5:0];
  //   Imm_Offset[15:0] = out_13[15:0]; IR[31:0] = out_13; PDA[25:0] = out_13[25:0]; ReadReg2[4:0] = out_13[20:16];
  //   ReadReg1[4:0] = out_13[25:21]; Op_code[5:0] = out_13[31:26]; NextPC[31:0] = out_15; PC[31:0] = out_14;
  //   ReadData1_ALUsrc1[31:0] = out_21; ReadData2_WriteDataMem[31:0] = out_22; WriteDataReg[31:0] = out_23;
  //   WriteReg[4:0] = out_19

  // Notes on the sheet:
  //   Enable
  //   PC+1
  //   R-TYPE
  //   LW
  //   LWM
  //   SW/BEQ
  //   J-TYPE
  //   JTA
  //   BTA
endmodule

module Instruction_Memory (
  input  [23:0] Address,
  input  Clock,
  input  Enable,
  output [31:0] Instruction
);

  RAM #(.addrWidth(24), .dataWidth(32)) ram_1 (
    .addr(Address), .data(Instruction), .clk(Clock), .ld(Enable));  // open: sel, clr

  // Notes on the sheet:
  //   Instruction Memory
endmodule

module Register_File (
  input  [4:0] ReadReg1,
  input  [4:0] ReadReg2,
  input  [4:0] WriteReg,
  input  [31:0] WriteData,
  input  Write,
  input  Clock,
  output [31:0] ReadData1,
  output [31:0] ReadData2
);

  wire and_1_out, and_2_out, and_3_out, and_4_out, and_5_out, and_6_out, and_7_out, and_8_out, and_9_out,
       and_10_out, and_11_out, and_12_out, and_13_out, and_14_out, and_15_out, and_16_out, and_17_out,
       and_18_out, and_19_out, and_20_out, and_21_out, and_22_out, and_23_out, and_24_out, and_25_out,
       and_26_out, and_27_out, and_28_out, and_29_out, and_30_out, and_31_out, and_32_out, decoder_1_out0,
       decoder_1_out1, decoder_1_out2, decoder_1_out3, decoder_1_out4, decoder_1_out5, decoder_1_out6,
       decoder_1_out7, decoder_1_out8, decoder_1_out9, decoder_1_out10, decoder_1_out11, decoder_1_out12,
       decoder_1_out13, decoder_1_out14, decoder_1_out15, decoder_1_out16, decoder_1_out17, decoder_1_out18,
       decoder_1_out19, decoder_1_out20, decoder_1_out21, decoder_1_out22, decoder_1_out23, decoder_1_out24,
       decoder_1_out25, decoder_1_out26, decoder_1_out27, decoder_1_out28, decoder_1_out29, decoder_1_out30,
       decoder_1_out31;
  wire [31:0] _0_q, _1_q, _2_q, _3_q, _4_q, _5_q, _6_q, _7_q, _8_q, _9_q, _10_q, _11_q, _12_q, _13_q, _14_q,
       _15_q, _16_q, _17_q, _18_q, _19_q, _20_q, _21_q, _22_q, _23_q, _24_q, _25_q, _26_q, _27_q, _28_q,
       _29_q, _30_q, _31_q;

  Decoder #(.select(5)) decoder_1 (
    .out0(decoder_1_out0), .out1(decoder_1_out1), .out2(decoder_1_out2), .out3(decoder_1_out3),
    .out4(decoder_1_out4), .out5(decoder_1_out5), .out6(decoder_1_out6), .out7(decoder_1_out7),
    .out8(decoder_1_out8), .out9(decoder_1_out9), .out10(decoder_1_out10), .out11(decoder_1_out11),
    .out12(decoder_1_out12), .out13(decoder_1_out13), .out14(decoder_1_out14), .out15(decoder_1_out15),
    .out16(decoder_1_out16), .out17(decoder_1_out17), .out18(decoder_1_out18), .out19(decoder_1_out19),
    .out20(decoder_1_out20), .out21(decoder_1_out21), .out22(decoder_1_out22), .out23(decoder_1_out23),
    .out24(decoder_1_out24), .out25(decoder_1_out25), .out26(decoder_1_out26), .out27(decoder_1_out27),
    .out28(decoder_1_out28), .out29(decoder_1_out29), .out30(decoder_1_out30), .out31(decoder_1_out31),
    .sel(WriteReg));  // open: en
  and and_1 (and_1_out, decoder_1_out0, Write);
  and and_2 (and_2_out, decoder_1_out1, Write);
  and and_3 (and_3_out, decoder_1_out2, Write);
  and and_4 (and_4_out, decoder_1_out3, Write);
  and and_5 (and_5_out, decoder_1_out4, Write);
  and and_6 (and_6_out, decoder_1_out5, Write);
  and and_7 (and_7_out, decoder_1_out6, Write);
  and and_8 (and_8_out, decoder_1_out7, Write);
  and and_9 (and_9_out, decoder_1_out8, Write);
  and and_10 (and_10_out, decoder_1_out9, Write);
  and and_11 (and_11_out, decoder_1_out10, Write);
  and and_12 (and_12_out, decoder_1_out11, Write);
  and and_13 (and_13_out, decoder_1_out12, Write);
  and and_14 (and_14_out, Write, decoder_1_out13);
  and and_15 (and_15_out, decoder_1_out14, Write);
  and and_16 (and_16_out, decoder_1_out15, Write);
  and and_17 (and_17_out, decoder_1_out16, Write);
  and and_18 (and_18_out, decoder_1_out17, Write);
  and and_19 (and_19_out, decoder_1_out18, Write);
  and and_20 (and_20_out, decoder_1_out19, Write);
  and and_21 (and_21_out, decoder_1_out20, Write);
  and and_22 (and_22_out, decoder_1_out21, Write);
  and and_23 (and_23_out, decoder_1_out22, Write);
  and and_24 (and_24_out, decoder_1_out23, Write);
  and and_25 (and_25_out, decoder_1_out24, Write);
  and and_26 (and_26_out, decoder_1_out25, Write);
  and and_27 (and_27_out, decoder_1_out26, Write);
  and and_28 (and_28_out, decoder_1_out27, Write);
  and and_29 (and_29_out, decoder_1_out28, Write);
  and and_30 (and_30_out, decoder_1_out29, Write);
  and and_31 (and_31_out, decoder_1_out30, Write);
  and and_32 (and_32_out, decoder_1_out31, Write);
  Register #(.width(32)) _0 (.D(WriteData), .en(and_1_out), .Q(_0_q), .clk(Clock));  // open: clr
  Register #(.width(32)) _1 (.D(WriteData), .en(and_2_out), .Q(_1_q), .clk(Clock));  // open: clr
  Register #(.width(32)) _2 (.D(WriteData), .en(and_3_out), .Q(_2_q), .clk(Clock));  // open: clr
  Register #(.width(32)) _3 (.D(WriteData), .en(and_4_out), .Q(_3_q), .clk(Clock));  // open: clr
  Register #(.width(32)) _4 (.D(WriteData), .en(and_5_out), .Q(_4_q), .clk(Clock));  // open: clr
  Register #(.width(32)) _5 (.D(WriteData), .en(and_6_out), .Q(_5_q), .clk(Clock));  // open: clr
  Register #(.width(32)) _6 (.D(WriteData), .en(and_7_out), .Q(_6_q), .clk(Clock));  // open: clr
  Register #(.width(32)) _7 (.D(WriteData), .en(and_8_out), .Q(_7_q), .clk(Clock));  // open: clr
  Register #(.width(32)) _8 (.D(WriteData), .en(and_9_out), .Q(_8_q), .clk(Clock));  // open: clr
  Register #(.width(32)) _9 (.D(WriteData), .en(and_10_out), .Q(_9_q), .clk(Clock));  // open: clr
  Register #(.width(32)) _10 (.D(WriteData), .en(and_11_out), .Q(_10_q), .clk(Clock));  // open: clr
  Register #(.width(32)) _11 (.D(WriteData), .en(and_12_out), .Q(_11_q), .clk(Clock));  // open: clr
  Register #(.width(32)) _12 (.D(WriteData), .en(and_13_out), .Q(_12_q), .clk(Clock));  // open: clr
  Register #(.width(32)) _13 (.D(WriteData), .en(and_14_out), .Q(_13_q), .clk(Clock));  // open: clr
  Register #(.width(32)) _14 (.D(WriteData), .en(and_15_out), .Q(_14_q), .clk(Clock));  // open: clr
  Register #(.width(32)) _15 (.D(WriteData), .en(and_16_out), .Q(_15_q), .clk(Clock));  // open: clr
  Register #(.width(32)) _16 (.D(WriteData), .en(and_17_out), .Q(_16_q), .clk(Clock));  // open: clr
  Register #(.width(32)) _17 (.D(WriteData), .en(and_18_out), .Q(_17_q), .clk(Clock));  // open: clr
  Register #(.width(32)) _18 (.D(WriteData), .en(and_19_out), .Q(_18_q), .clk(Clock));  // open: clr
  Register #(.width(32)) _19 (.D(WriteData), .en(and_20_out), .Q(_19_q), .clk(Clock));  // open: clr
  Register #(.width(32)) _20 (.D(WriteData), .en(and_21_out), .Q(_20_q), .clk(Clock));  // open: clr
  Register #(.width(32)) _21 (.D(WriteData), .en(and_22_out), .Q(_21_q), .clk(Clock));  // open: clr
  Register #(.width(32)) _22 (.D(WriteData), .en(and_23_out), .Q(_22_q), .clk(Clock));  // open: clr
  Register #(.width(32)) _23 (.D(WriteData), .en(and_24_out), .Q(_23_q), .clk(Clock));  // open: clr
  Register #(.width(32)) _24 (.D(WriteData), .en(and_25_out), .Q(_24_q), .clk(Clock));  // open: clr
  Register #(.width(32)) _25 (.D(WriteData), .en(and_26_out), .Q(_25_q), .clk(Clock));  // open: clr
  Register #(.width(32)) _26 (.D(WriteData), .en(and_27_out), .Q(_26_q), .clk(Clock));  // open: clr
  Register #(.width(32)) _27 (.D(WriteData), .en(and_28_out), .Q(_27_q), .clk(Clock));  // open: clr
  Register #(.width(32)) _28 (.D(WriteData), .en(and_29_out), .Q(_28_q), .clk(Clock));  // open: clr
  Register #(.width(32)) _29 (.D(WriteData), .en(and_30_out), .Q(_29_q), .clk(Clock));  // open: clr
  Register #(.width(32)) _30 (.D(WriteData), .en(and_31_out), .Q(_30_q), .clk(Clock));  // open: clr
  Register #(.width(32)) _31 (.D(WriteData), .en(and_32_out), .Q(_31_q), .clk(Clock));  // open: clr
  Multiplexer #(.select(5), .width(32)) multiplexer_1 (
    .in0(_0_q), .in1(_1_q), .in2(_2_q), .in3(_3_q), .in4(_4_q), .in5(_5_q), .in6(_6_q), .in7(_7_q),
    .in8(_8_q), .in9(_9_q), .in10(_10_q), .in11(_11_q), .in12(_12_q), .in13(_13_q), .in14(_14_q),
    .in15(_15_q), .in16(_16_q), .in17(_17_q), .in18(_18_q), .in19(_19_q), .in20(_20_q), .in21(_21_q),
    .in22(_22_q), .in23(_23_q), .in24(_24_q), .in25(_25_q), .in26(_26_q), .in27(_27_q), .in28(_28_q),
    .in29(_29_q), .in30(_30_q), .in31(_31_q), .out(ReadData1), .sel(ReadReg1));  // open: en
  Multiplexer #(.select(5), .width(32)) multiplexer_2 (
    .in0(_0_q), .in1(_1_q), .in2(_2_q), .in3(_3_q), .in4(_4_q), .in5(_5_q), .in6(_6_q), .in7(_7_q),
    .in8(_8_q), .in9(_9_q), .in10(_10_q), .in11(_11_q), .in12(_12_q), .in13(_13_q), .in14(_14_q),
    .in15(_15_q), .in16(_16_q), .in17(_17_q), .in18(_18_q), .in19(_19_q), .in20(_20_q), .in21(_21_q),
    .in22(_22_q), .in23(_23_q), .in24(_24_q), .in25(_25_q), .in26(_26_q), .in27(_27_q), .in28(_28_q),
    .in29(_29_q), .in30(_30_q), .in31(_31_q), .out(ReadData2), .sel(ReadReg2));  // open: en
endmodule

module ALU (
  input  [2:0] ALUOperation,
  input  [31:0] Src1,
  input  [31:0] Src2,
  output Zero_Flag,
  output [31:0] ALU_Result
);

  wire subtractor_1_bout;
  wire [31:0] adder_1_out, adder_2_out, and_1_out, bit_extender_1_out, not_1_out, or_1_out;

  assign not_1_out = ~Src2;  // NOT_Gate not_1, 32 bits wide
  assign and_1_out = Src1 & Src2;  // AND_Gate and_1, 32 bits wide
  assign or_1_out = Src1 | Src2;  // OR_Gate or_1, 32 bits wide
  Adder #(.width(32)) adder_1 (.a(Src1), .b(Src2), .out(adder_1_out));  // open: cin, cout
  Adder #(.width(32)) adder_2 (.a(Src1), .b(not_1_out), .out(adder_2_out), .cin(1'b1));  // open: cout
  Subtractor #(.width(32)) subtractor_1 (.a(Src1), .b(Src2), .bin(1'b0), .bout(subtractor_1_bout));  // open: out
  assign bit_extender_1_out = {{31{1'b0}}, subtractor_1_bout};  // Bit_Extender bit_extender_1
  Multiplexer #(.select(3), .width(32)) multiplexer_1 (
    .in0(and_1_out), .in1(or_1_out), .in2(adder_1_out), .in6(adder_2_out), .in7(bit_extender_1_out),
    .out(ALU_Result), .sel(ALUOperation));  // open: in3, in4, in5, en
  nor nor_1 (Zero_Flag, ALU_Result[0], ALU_Result[1], ALU_Result[2], ALU_Result[3], ALU_Result[4], ALU_Result[5], ALU_Result[6], ALU_Result[7], ALU_Result[8], ALU_Result[9], ALU_Result[10], ALU_Result[11], ALU_Result[12], ALU_Result[13], ALU_Result[14], ALU_Result[15], ALU_Result[16], ALU_Result[17], ALU_Result[18], ALU_Result[19], ALU_Result[20], ALU_Result[21], ALU_Result[22], ALU_Result[23], ALU_Result[24], ALU_Result[25], ALU_Result[26], ALU_Result[27], ALU_Result[28], ALU_Result[29], ALU_Result[30], ALU_Result[31]);

  // Notes on the sheet:
  //   AND
  //   OR
  //   Adder
  //   Subtractor
  //   slt
endmodule

module Data_Memory (
  input  [23:0] Address,
  input  MemWrite,
  input  MemRead,
  input  [31:0] WriteData,
  input  Clock,
  output [31:0] ReadData
);

  RAM #(.addrWidth(24), .dataWidth(32), .bus("separate")) ram_1 (
    .addr(Address), .din(WriteData), .data(ReadData), .str(MemWrite), .clk(Clock), .ld(MemRead));  // open: sel, clr
endmodule

module ALU_Control (
  input  [1:0] ALUop,
  input  [5:0] Instruction_5_0,
  output [2:0] ALUOperation
);

  wire and_1_out, not_1_out, not_2_out, or_1_out;

  and and_1 (and_1_out, ALUop[1], Instruction_5_0[1]);
  or or_1 (or_1_out, Instruction_5_0[3], Instruction_5_0[0]);
  not not_1 (not_1_out, ALUop[1]);
  not not_2 (not_2_out, Instruction_5_0[2]);
  or or_2 (ALUOperation[2], ALUop[0], and_1_out);
  or or_3 (ALUOperation[1], not_1_out, not_2_out);
  and and_2 (ALUOperation[0], ALUop[1], or_1_out);
endmodule

module Control_Unit (
  input  [5:0] Instruction_31_26,
  output RegWrite,
  output ALUsrc,
  output MemWrite,
  output Branch,
  output lwmadd,
  output RegDst,
  output [1:0] ALUOp,
  output MemRead,
  output MemToReg,
  output Jump
);

  wire lw_out, Op0_out, Op1_out, Op2_out, Op3_out, Op4_out, Op5_out;

  not Op5 (Op5_out, Instruction_31_26[5]);
  not Op4 (Op4_out, Instruction_31_26[4]);
  not Op3 (Op3_out, Instruction_31_26[3]);
  not Op2 (Op2_out, Instruction_31_26[2]);
  not Op0 (Op0_out, Instruction_31_26[0]);
  not Op1 (Op1_out, Instruction_31_26[1]);
  and R (ALUOp[1], Op5_out, Op4_out, Op3_out, Op2_out, Op1_out, Op0_out);
  and lw (lw_out, Instruction_31_26[5], Op4_out, Op3_out, Op2_out, Instruction_31_26[1], Instruction_31_26[0]);
  and sw (MemWrite, Instruction_31_26[5], Op4_out, Instruction_31_26[3], Op2_out, Instruction_31_26[1], Instruction_31_26[0]);
  and beq (ALUOp[0], Op5_out, Op4_out, Op3_out, Instruction_31_26[2], Op1_out, Op0_out);
  and j (Jump, Op5_out, Op4_out, Op3_out, Op2_out, Instruction_31_26[1], Op0_out);
  and lwm (lwmadd, Op5_out, Op4_out, Instruction_31_26[3], Instruction_31_26[2], Op1_out, Op0_out);
  or or_1 (RegWrite, ALUOp[1], lw_out, lwmadd);
  or or_2 (ALUsrc, lw_out, MemWrite);
  or or_3 (MemRead, lw_out, lwmadd);
  or or_4 (MemToReg, lw_out, lwmadd);

  assign Branch = ALUOp[0];
  assign RegDst = ALUOp[1];
endmodule
